// Logisim project lab_1.circ as structural Verilog: 1 circuit, main circuit NOT/AND/OR
module NOT_AND_OR (
  input  A,
  input  in_2,
  input  in_3,
  input  A_2,
  input  A_3,
  input  B,
  input  B_2,
  input  in_8,
  input  in_9,
  output C,
  output C_2,
  output C_3,
  output out_13,
  output out_14
);

  wire transistor_3_out, transistor_8_out, transistor_14_out, transistor_15_out;

  Transistor transistor_1 (.in(1'b1), .out(C), .gate(A_2));
  Transistor #(.\type ("n")) transistor_2 (.in(1'b0), .out(C), .gate(A_2));
  Transistor #(.\type ("n")) transistor_3 (.in(1'b1), .out(transistor_3_out), .gate(A_3));
  Transistor #(.\type ("n")) transistor_4 (.in(transistor_3_out), .out(C_2), .gate(B));
  Transistor transistor_5 (.in(1'b0), .out(C_2), .gate(A_3));
  Transistor transistor_6 (.in(1'b0), .out(C_2), .gate(B));
  Transistor #(.\type ("n")) transistor_7 (.in(1'b1), .out(C_3), .gate(A));
  Transistor transistor_8 (.in(1'b0), .out(transistor_8_out), .gate(B_2));
  Transistor #(.\type ("n")) transistor_9 (.in(1'b1), .out(C_3), .gate(B_2));
  Transistor transistor_10 (.in(transistor_8_out), .out(C_3), .gate(A));
  Transistor transistor_11 (.in(1'b1), .out(out_13), .gate(in_2));
  Transistor transistor_12 (.in(1'b1), .out(out_13), .gate(in_8));
  Transistor #(.\type ("n")) transistor_13 (.in(transistor_14_out), .out(out_13), .gate(in_2));
  Transistor #(.\type ("n")) transistor_14 (.in(1'b0), .out(transistor_14_out), .gate(in_8));
  Transistor transistor_15 (.in(1'b1), .out(transistor_15_out), .gate(in_3));
  Transistor transistor_16 (.in(transistor_15_out), .out(out_14), .gate(in_9));
  Transistor #(.\type ("n")) transistor_17 (.in(1'b0), .out(out_14), .gate(in_3));
  Transistor #(.\type ("n")) transistor_18 (.in(1'b0), .out(out_14), .gate(in_9));

  // Notes on the sheet:
  //   OR
  //   AND
  //   OR
  //   AND-NOT
  //   OR-NOT
endmodule
