// Logisim project lights.circ as structural Verilog: 5 circuits, main circuit input logic
module input_logic (
  input  s1,
  input  s0,
  input  ta,
  input  tb,
  output fs1,
  output fs0
);

  wire and_1_out, and_2_out, and_3_out, and_4_out, not_1_out, not_2_out, not_3_out, not_4_out, not_5_out,
       not_6_out, not_7_out;

  not not_1 (not_1_out, s1);
  and and_1 (and_1_out, not_1_out, s0);
  and and_2 (and_2_out, s1, not_2_out);
  not not_2 (not_2_out, s0);
  not not_3 (not_3_out, s1);
  and and_3 (and_3_out, not_3_out, not_4_out, not_5_out);
  not not_4 (not_4_out, s0);
  not not_5 (not_5_out, ta);
  not not_6 (not_6_out, s0);
  and and_4 (and_4_out, s1, not_6_out, not_7_out);
  not not_7 (not_7_out, tb);
  or or_1 (fs1, and_1_out, and_2_out);
  or or_2 (fs0, and_3_out, and_4_out);

  // Notes on the sheet:
  //   Состояния
  //   Кнопки
endmodule

module llights (
  input  \Сброс ,
  output [2:0] out_2
);

  wire button_1_out, button_2_out, buttons_1_out_5, buttons_1_out_6, clock_1_out, input_logic_1_fs0,
       input_logic_1_fs1, lights_logic_1_green_1, lights_logic_1_green_2, lights_logic_1_green_p_1,
       lights_logic_1_green_p_2, lights_logic_1_orange_1, lights_logic_1_orange_2, lights_logic_1_red_1,
       lights_logic_1_red_2, lights_logic_1_red_p_1, lights_logic_1_red_p_2, ram_1_out_5, ram_1_out_6,
       ram_1_out_8, ram_1_out_9;

  Button button_1 (.out(button_1_out));
  Button button_2 (.out(button_2_out));
  input_logic input_logic_1 (
    .s1(ram_1_out_6), .s0(ram_1_out_5), .ta(buttons_1_out_6), .tb(buttons_1_out_5), .fs1(input_logic_1_fs1),
    .fs0(input_logic_1_fs0));
  buttons buttons_1 (
    .in_1(button_1_out), .in_3(button_2_out), .in_2(lights_logic_1_green_p_1),
    .in_4(lights_logic_1_green_p_2), .out_6(buttons_1_out_6), .out_5(buttons_1_out_5));
  Clock clock_1 (.out(clock_1_out));
  ram ram_1 (
    .in_1(input_logic_1_fs1), .in_2(input_logic_1_fs0), .out_7(out_2), .out_8(ram_1_out_8),
    .out_9(ram_1_out_9), .out_5(ram_1_out_5), .out_6(ram_1_out_6), .\для_генератора (clock_1_out),
    .in_3(\Сброс ));
  LED led_1 (.in(lights_logic_1_red_p_1));
  LED led_2 (.in(lights_logic_1_green_p_1));
  LED led_3 (.in(lights_logic_1_red_p_2));
  LED led_4 (.in(lights_logic_1_green_p_2));
  LED led_5 (.in(lights_logic_1_red_1));
  LED led_6 (.in(lights_logic_1_orange_1));
  LED led_7 (.in(lights_logic_1_green_1));
  LED led_8 (.in(lights_logic_1_red_2));
  lights_logic lights_logic_1 (
    .in_1(ram_1_out_8), .in_2(ram_1_out_9), .green_1(lights_logic_1_green_1),
    .orange_1(lights_logic_1_orange_1), .red_1(lights_logic_1_red_1), .green_p_1(lights_logic_1_green_p_1),
    .red_p_1(lights_logic_1_red_p_1), .green_2(lights_logic_1_green_2), .orange_2(lights_logic_1_orange_2),
    .red_2(lights_logic_1_red_2), .green_p_2(lights_logic_1_green_p_2), .red_p_2(lights_logic_1_red_p_2));
  LED led_9 (.in(lights_logic_1_orange_2));
  LED led_10 (.in(lights_logic_1_green_2));
endmodule

module lights_logic (
  input  in_1,
  input  in_2,
  output green_1,
  output orange_1,
  output red_1,
  output green_p_1,
  output red_p_1,
  output green_2,
  output orange_2,
  output red_2,
  output green_p_2,
  output red_p_2
);

  wire not_1_out, not_3_out, not_4_out, not_5_out, not_6_out;

  not not_1 (not_1_out, in_1);
  and and_1 (green_2, in_1, in_2);
  not not_2 (green_p_2, in_1);
  and and_2 (green_1, not_1_out, in_2);
  not not_3 (not_3_out, green_1);
  and and_3 (orange_1, not_3_out, not_4_out);
  not not_4 (not_4_out, in_1);
  not not_5 (not_5_out, green_p_2);
  not not_6 (not_6_out, green_2);
  and and_4 (orange_2, not_5_out, not_6_out);
  or or_1 (red_p_1, green_1, orange_1);

  assign green_p_1 = in_1;
  assign red_1 = in_1;
  assign red_2 = green_p_2;
  assign red_p_2 = green_2;
endmodule

module ram (
  input  in_1,
  input  in_2,
  input  in_3,
  input  \для_генератора ,
  output out_5,
  output out_6,
  output [2:0] out_7,
  output out_8,
  output out_9
);

  wire counter_1_carry;

  Counter #(.width(3), .max('h4)) counter_1 (
    .Q(out_7), .carry(counter_1_carry), .clk(\для_генератора ));  // open: load, D, count, clr
  D_Flip_Flop d_ff_1 (.clk(counter_1_carry), .D(in_1), .Q(out_6), .Qn(out_8), .reset(in_3));  // open: preset, en
  D_Flip_Flop d_ff_2 (.clk(counter_1_carry), .D(in_2), .Q(out_5), .Qn(out_9), .reset(in_3));  // open: preset, en
endmodule

module buttons (
  input  in_1,
  input  in_2,
  input  in_3,
  input  in_4,
  output out_5,
  output out_6
);

  wire t_ff_1_qn, t_ff_2_qn;

  T_Flip_Flop t_ff_1 (.clk(in_1), .T(t_ff_1_qn), .Q(out_5), .Qn(t_ff_1_qn), .reset(in_2));  // open: preset, en
  T_Flip_Flop t_ff_2 (.clk(in_3), .T(t_ff_2_qn), .Q(out_6), .Qn(t_ff_2_qn), .reset(in_4));  // open: preset, en
endmodule
